# Fritzing sketch opti-hda2 (saved by Fritzing 0.9.3b)
circuit board: 10cm x 11.5cm
breadboards: 1

parts:
  RTC_Left = female pin header, 6 pins [form="♀ (female)"]  # not connected
  J5 = double row female pin header, 2 pins [form="♀ (female)"]
  J6 = double row female pin header, 2 pins [form="♀ (female)"]
  J7 = double row female pin header, 2 pins [form="♀ (female)"]
  J8 = double row female pin header, 2 pins [form="♀ (female)"]
  J9 = double row female pin header, 2 pins [form="♀ (female)"]
  J11 = double row female pin header, 2 pins [form="♀ (female)"]
  J12 = double row female pin header, 2 pins [form="♀ (female)"]
  J16 = female pin header, 1 pin [form="♀ (female)"]
  J17 = female pin header, 1 pin [form="♀ (female)"]
  J18 = female pin header, 1 pin [form="♀ (female)"]
  J19 = female pin header, 1 pin [form="♀ (female)"]
  J23 = female pin header, 1 pin [form="♀ (female)"]
  J24 = female pin header, 1 pin [form="♀ (female)"]
  J25 = female pin header, 1 pin [form="♀ (female)"]
  J26 = female pin header, 1 pin [form="♀ (female)"]
  J27 = female pin header, 1 pin [form="♀ (female)"]
  J30 = female pin header, 1 pin [form="♀ (female)"]
  J31 = female pin header, 1 pin [form="♀ (female)"]
  J33 = female pin header, 1 pin [form="♀ (female)"]
  J22 = female pin header, 1 pin [form="♀ (female)"]
  J37 = female pin header, 1 pin [form="♀ (female)"]
  J40 = female pin header, 1 pin [form="♀ (female)"]
  R1 = Resistor [tolerance=±5% resistance=220 package="1206 [SMD]"]
  R2 = Resistor [tolerance=±5% resistance=220 package="1206 [SMD]"]
  R5 = Resistor [tolerance=±5% resistance=220 package="1206 [SMD]"]
  R4 = Resistor [tolerance=±5% resistance=220 package="1206 [SMD]"]
  R3 = Resistor [tolerance=±5% resistance=220 package="1206 [SMD]"]
  USB = USB Connectors [package=usb-b-pth]
  DB9 = DB9 Connector [package=db9]
  J2 = double row rounded female pin header, 44 pins [form="♀ (female rounded)"]
  J36 = double row female pin header, 4 pins [form="♀ (female)"]  # not connected
  J35 = double row female pin header, 16 pins [form="♀ (female)"]  # not connected
  J1 = double row rounded female pin header, 44 pins [form="♀ (female rounded)"]
  J34 = female pin header, 1 pin [form="♀ (female)"]
  J32 = female pin header, 1 pin [form="♀ (female)"]
  J41 = female pin header, 1 pin [form="♀ (female)"]
  J38 = female pin header, 1 pin [form="♀ (female)"]
  J39 = female pin header, 1 pin [form="♀ (female)"]
  J42 = female pin header, 1 pin [form="♀ (female)"]
  J43 = female pin header, 1 pin [form="♀ (female)"]
  RTC_Right = female pin header, 6 pins [form="♀ (female)"]
  LTE/GPS = female pin header, 7 pins [form="♀ (female)"]
  J46 = female pin header, 2 pins [form="♀ (female)"]
  J47 = female pin header, 1 pin [form="♀ (female)"]
  Micro_SD = female pin header, 8 pins [form="♀ (female)"]
  J45 = female pin header, 1 pin [form="♀ (female)"]
  RTC_Left1 = female pin header, 4 pins [form="♀ (female)"]
  J50 = double row female pin header, 2 pins [form="♀ (female)"]
  Micro_SD1 = female pin header, 8 pins [form="♀ (female)"]
  J51 = female pin header, 4 pins [form="♀ (female)"]
  J54 = female pin header, 1 pin [form="♀ (female)"]
  R6 = Resistor [tolerance=±5% resistance=220 package="1206 [SMD]"]
  J56 = female pin header, 1 pin [form="♀ (female)"]
  J57 = female pin header, 1 pin [form="♀ (female)"]
  J58 = female pin header, 1 pin [form="♀ (female)"]
  J59 = female pin header, 1 pin [form="♀ (female)"]
  J60 = female pin header, 1 pin [form="♀ (female)"]
  IC = 24LC01 [package="SO8 [SMD]"]
  J10 = double row female pin header, 2 pins [form="♀ (female)"]
  J62 = female pin header, 1 pin [form="♀ (female)"]
  R7 = Resistor [tolerance=±5% resistance=220 package="1206 [SMD]"]
  R8 = Resistor [tolerance=±5% resistance=220 package="1206 [SMD]"]
  J49 = double row female pin header, 4 pins [form="♀ (female)"]
  J63 = female pin header, 1 pin [form="♀ (female)"]
  J64 = female pin header, 1 pin [form="♀ (female)"]
  SJ1 = Solder Jumper [package=sj_2s-trace]
  SJ2 = Solder Jumper [package=sj_2s-trace]
  SJ3 = Solder Jumper [package=sj_2s-trace]
  SJ4 = Solder Jumper [package=sj_2s-trace]

nets:
  N1: J5.pin1, J5.pin2, J9.pin1, J9.pin2, DB9.2, SJ1.2, SJ2.1
  N2: J6.pin1, J6.pin2, J2.pin1, LTE/GPS.pin2
  N3: J7.pin1, J7.pin2
  N4: J8.pin1, J8.pin2, LTE/GPS.pin3, J62.pin1
  N5: J11.pin1, J11.pin2, J46.pin1, J47.pin1
  N6: J12.pin1, J12.pin2, J46.pin2
  N7: J16.pin1, DB9.9
  N8: J17.pin1, DB9.5
  N9: J18.pin1, R5.Pin_0, IC.SCL_-_I2C_Clock
  N10: J19.pin1, J1.pin25
  N11: J23.pin1, IC.WP_-_Write_Protect, SJ4.2
  N12: J24.pin1, DB9.3
  N13: J25.pin1, J1.pin34
  N14: J26.pin1, RTC_Right.pin5, R8.Pin_1
  N15: J27.pin1, J43.pin1, RTC_Right.pin3
  N16: J30.pin1, RTC_Right.pin2, Micro_SD.pin7, Micro_SD1.pin7, J56.pin1, IC.A2, R7.Pin_0, R8.Pin_0
  N17: J31.pin1, J40.pin1
  N18: J33.pin1, Micro_SD.pin3, Micro_SD1.pin3
  N19: J22.pin1, IC.A0
  N20: J37.pin1, IC.0V
  N21: R1.Pin_0, J2.pin8
  N22: R1.Pin_1, RTC_Left1.pin4
  N23: R2.Pin_0, J2.pin7
  N24: R2.Pin_1, RTC_Left1.pin3
  N25: R5.Pin_1, SJ4.1
  N26: R4.Pin_0, J42.pin1, Micro_SD.pin6, Micro_SD1.pin6, IC.A1
  N27: R4.Pin_1, IC.+V
  N28: R3.Pin_0, J2.pin6
  N29: R3.Pin_1, RTC_Left1.pin1
  N30: USB.D+, J49.pin4
  N31: USB.D-, J49.pin1
  N32: USB.GND, J49.pin3
  N33: USB.VBUS, J50.pin2
  N34: DB9.1, SJ1.1
  N35: J2.pin5, J59.pin1
  N36: J1.pin6, Micro_SD.pin5, Micro_SD1.pin5
  N37: J1.pin7, Micro_SD.pin4, Micro_SD1.pin4
  N38: J1.pin12, J38.pin1
  N39: J1.pin16, J41.pin1
  N40: J1.pin20, J39.pin1
  N41: J1.pin29, LTE/GPS.pin5
  N42: J1.pin39, J34.pin1
  N43: J1.pin40, Micro_SD.pin2, Micro_SD1.pin2
  N44: J32.pin1, LTE/GPS.pin6
  N45: RTC_Right.pin4, R7.Pin_1
  N46: Micro_SD.pin1, Micro_SD1.pin1
  N47: Micro_SD.pin8, Micro_SD1.pin8
  N48: J45.pin1, RTC_Left1.pin2, SJ2.2
  N49: J50.pin1, J49.pin2
  N50: J51.pin1, R6.Pin_0, J57.pin1
  N51: J51.pin2, R6.Pin_1, SJ3.1
  N52: J51.pin3, SJ3.2
  N53: J51.pin4, J54.pin1
  N54: J58.pin1, J60.pin1
  N55: J10.pin1, J10.pin2
  N56: J63.pin1, J64.pin1

notes:
  OPTI-HDA2
